# Fritzing sketch project-1 (saved by Fritzing 1.0.1rc)
breadboards: 1

parts:
  Mod1 = Heltec WiFi LoRa 32 V2 [part_number=HTIT-WB32LA]
  LED1 = LEDs [package=led10mm]
  LED2 = LEDs [package=led10mm]
  LED3 = LEDs [package=led10mm]
  R1 = Resistor [tolerance=±5% power=0.25W resistance=220 package=THT]
  R2 = Resistor [tolerance=±5% power=0.25W resistance=220 package=THT]
  R3 = Resistor [tolerance=±5% power=0.25W resistance=220 package=THT]

nets:
  N1: Mod1.pin_2, R3.Pin_0
  N2: Mod1.pin_16, Mod1.pin_17
  N3: Mod1.GND, LED1.A, LED2.A, LED3.A
  N4: Mod1.pin_21, Mod1.pin_22
  N5: Mod1.pin_32, R2.Pin_0
  N6: Mod1.pin_33, R1.Pin_0
  N7: LED1.C, R1.Pin_1
  N8: LED2.C, R2.Pin_1
  N9: LED3.C, R3.Pin_1
