# Fritzing sketch project-2 (saved by Fritzing 1.0.1rc)
circuit board: 8.46667cm x 5.64444cm
breadboards: 1

parts:
  Mod1 = Heltec WiFi LoRa 32 V2 [part_number=HTIT-WB32LA]
  LED1 = LEDs [package=led10mm]
  R1 = Resistor [tolerance=±5% power=0.25W resistance=220 package=THT]
  S1 = Pushbutton [package="[THT]"]
  R2 = Resistor [tolerance=±5% power=0.25W resistance=10k package=THT]
  R3 = Resistor [tolerance=±5% power=0.25W resistance=10k package=THT]
  S2 = Pushbutton [package="[THT]"]
  R4 = Resistor [tolerance=±5% power=0.25W resistance=10k package=THT]
  R5 = Resistor [tolerance=±5% power=0.25W resistance=10k package=THT]

nets:
  N1: Mod1.pin_2, R4.Pin_0
  N2: Mod1.pin_3, R2.Pin_0
  N3: Mod1.pin_16, Mod1.pin_17, R3.Pin_0, R5.Pin_0
  N4: Mod1.GND, LED1.A, S1.Pin_1, S1.Pin_2, S2.Pin_1, S2.Pin_2
  N5: Mod1.pin_21, Mod1.pin_22
  N6: Mod1.pin_33, R1.Pin_0
  N7: LED1.C, R1.Pin_1
  N8: S1.Pin_3, S1.Pin_4, R4.Pin_1, R5.Pin_1
  N9: R2.Pin_1, R3.Pin_1, S2.Pin_3, S2.Pin_4
