# Fritzing sketch lab-2-project-1 (saved by Fritzing 1.0.1rc)
breadboards: 1

parts:
  R6 = Resistor [tolerance=±5% power=0.25W resistance=220 package=THT]
  S3 = Pushbutton [package="[THT]"]
  S4 = Pushbutton [package="[THT]"]
  R8 = Resistor [tolerance=±5% power=0.25W resistance=220 package=THT]
  R9 = Resistor [tolerance=±5% power=0.25W resistance=220 package=THT]
  R10 = Resistor [tolerance=±5% power=0.25W resistance=220 package=THT]
  Mod2 = Heltec WiFi LoRa 32 V2 [part_number=HTIT-WB32LA]
  D1 = LED_BARGRAPH_10 [package=led_bargaph_10]
  R12 = Resistor [tolerance=±5% power=0.25W resistance=220 package=THT]
  R13 = Resistor [tolerance=±5% power=0.25W resistance=220 package=THT]
  R14 = Resistor [tolerance=±5% power=0.25W resistance=220 package=THT]
  R15 = Resistor [tolerance=±5% power=0.25W resistance=220 package=THT]
  R16 = Resistor [tolerance=±5% power=0.25W resistance=220 package=THT]
  R19 = Resistor [tolerance=±5% power=0.25W resistance=220 package=THT]
  R20 = Resistor [tolerance=±5% power=0.25W resistance=220 package=THT]
  R21 = Resistor [tolerance=±5% power=0.25W resistance=220 package=THT]

nets:
  N1: R6.Pin_0, Mod2.pin_16, Mod2.pin_17, R21.Pin_0
  N2: R6.Pin_1, S3.Pin_1, S3.Pin_2, S4.Pin_1, S4.Pin_2, R9.Pin_0, Mod2.GND, R12.Pin_0, R13.Pin_0, R14.Pin_0, R15.Pin_0, R16.Pin_0, R19.Pin_0, R20.Pin_0, R21.Pin_1
  N3: S3.Pin_3, S3.Pin_4, R8.Pin_1
  N4: S4.Pin_3, S4.Pin_4, R10.Pin_1
  N5: R8.Pin_0, Mod2.pin_3
  N6: R9.Pin_1, D1.J_A
  N7: R10.Pin_0, Mod2.pin_2
  N8: Mod2.pin_21, Mod2.pin_22
  N9: Mod2.pin_26, D1.H_C
  N10: Mod2.pin_27, D1.C_C
  N11: Mod2.pin_28, D1.D_C
  N12: Mod2.pin_30, D1.E_C
  N13: Mod2.pin_31, D1.F_C
  N14: Mod2.pin_32, D1.J_C
  N15: Mod2.pin_33, D1.I_C
  N16: Mod2.pin_34, D1.G_C
  N17: D1.C_A, R16.Pin_1
  N18: D1.D_A, R15.Pin_1
  N19: D1.E_A, R14.Pin_1
  N20: D1.F_A, R13.Pin_1
  N21: D1.G_A, R12.Pin_1
  N22: D1.H_A, R19.Pin_1
  N23: D1.I_A, R20.Pin_1
