# Fritzing sketch project-2 (saved by Fritzing 1.0.1rc)
breadboards: 1

parts:
  R23 = Resistor [tolerance=±5% power=0.25W resistance=220 package=THT]
  S5 = Pushbutton [package="[THT]"]
  R30 = Resistor [tolerance=±5% power=0.25W resistance=220 package=THT]
  RGB_LED = RGB LED - (4 legs) [color="Red (633nm)" current=0.030A package="5 mm [THT]"]
  R31 = Resistor [tolerance=±5% power=0.25W resistance=220 package=THT]
  R32 = Resistor [tolerance=±5% power=0.25W resistance=220 package=THT]
  R33 = Resistor [tolerance=±5% power=0.25W resistance=220 package=THT]
  Mod3 = Heltec WiFi LoRa 32 V2 [part_number=HTIT-WB32LA]
  Part1 = 12 NeoPixel Ring [part_number=1643]

nets (from the schematic view):
  N1: R23.Pin_0, RGB_LED.green_cathode, Mod3.pin_16, Mod3.pin_17, Part1.VDD
  GND: R23.Pin_1, S5.Pin_1, S5.Pin_2, Mod3.GND, Part1.GND
  N2: S5.Pin_3, S5.Pin_4, R30.Pin_1
  N3: R30.Pin_0, Mod3.pin_3
  N4: RGB_LED.red_cathode, R32.Pin_0
  N5: RGB_LED.common_anode, R31.Pin_0
  N6: RGB_LED.blue_cathode, R33.Pin_0
  N7: R31.Pin_1, Mod3.pin_33
  N8: R32.Pin_1, Mod3.pin_26
  N9: R33.Pin_1, Mod3.pin_32
  N10: Mod3.pin_21, Mod3.pin_22
  N11: Mod3.pin_31, Part1.IN

custom parts:
  12 NeoPixel Ring: 12 ultra bright smart LED NeoPixels are arranged in a circle with 1.5" (37mm) outer diameter. The rings are 'chainable' - connect the output pin of one to the input pin of another. Use only one microcontroller pin to control as many as you can chain together! Each LED is addressable as the driver chip is inside the LED. Each one has ~18mA constant current drive so the color will be very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
